// Logisim project Final_Project.circ as structural Verilog
module TestBench (
  input  [7:0] Address,
  input  JumpToAddress
);

  wire button_1_out, clock_1_out, comparator_1_eq;
  wire [3:0] rom_1_data_2;
  wire [7:0] alu_1_result, counter_1_q;
  wire [15:0] rom_1_data;

  Clock clock_1 (.out(clock_1_out));
  Button button_1 (.out(button_1_out));
  ROM #(.dataWidth(20)) rom_1 (.addr(counter_1_q), .data({rom_1_data_2, rom_1_data}));
  Counter counter_1 (
    .load(JumpToAddress), .D(Address), .count(1'b1), .Q(counter_1_q), .up(1'b1), .clk(clock_1_out),
    .clr(button_1_out));  // open: carry
  Hex_Digit_Display #(.decimalPoint("false")) Operation (.value(rom_1_data_2));
  Hex_Digit_Display #(.decimalPoint("false")) hex_digit_display_1 (.value(rom_1_data[15:12]));
  Hex_Digit_Display #(.decimalPoint("false")) hex_digit_display_2 (.value(rom_1_data[11:8]));
  ALU alu_1 (
    .Result(alu_1_result), .Operand1(rom_1_data[15:12]), .Operand2(rom_1_data[11:8]), .Operation(rom_1_data_2));
  Hex_Digit_Display #(.decimalPoint("false")) hex_digit_display_3 (.value(alu_1_result[7:4]));
  Hex_Digit_Display #(.decimalPoint("false")) hex_digit_display_4 (.value(alu_1_result[3:0]));
  LED led_1 (.in(comparator_1_eq));
  Comparator comparator_1 (.a(alu_1_result), .b(rom_1_data[7:0]), .eq(comparator_1_eq));  // open: gt, lt

  // Notes on the sheet:
  //   Clock
  //   Restart
  //   contents of rom_1 (hex, n*v repeats v):
  //   a00a 1a0f6 10000 21203 2af19 3fa05 3affb 4340c 4ffe1 8a0f5 800ff 9a302 aa30b ba309 cf00f cf378 cf780
  //   cf800 df00f df301 df400 df800
  //   Operation
  //   Operand 1
  //   Don't Modify This Testbench
  //   Operand 2
  //   Result
  //   OK
endmodule

module ALU (
  input  [3:0] Operand1,
  input  [3:0] Operand2,
  input  [3:0] Operation,
  output [7:0] Result
);

  wire [3:0] move_1_out_2, negative_1_o1;
  wire [4:0] four_bits_adder_1_sum1, four_bits_subtractor_1_sum1;
  wire [7:0] and_op_1_andop, bit_extender_1_out, bit_extender_2_out, bit_extender_3_out, bit_extender_4_out,
       bit_extender_5_out, bit_extender_6_out, multiplication_1_r1, mux16x1shiftr_1_out_3, not_op_1_not_op1,
       or4bites_1_out_3, shiftleft_1_out_3, xor4bites_1_out_3;

  assign bit_extender_1_out = {{4{1'b0}}, Operand1};  // Bit_Extender bit_extender_1
  assign bit_extender_2_out = {{4{1'b0}}, Operand2};  // Bit_Extender bit_extender_2
  Negative negative_1 (
    .A4(Operand1[3]), .A3(Operand1[2]), .A2(Operand1[1]), .A1(Operand1[0]), .O4(negative_1_o1[3]),
    .O3(negative_1_o1[2]), .O2(negative_1_o1[1]), .O1(negative_1_o1[0]));
  not_op not_op_1 (.op1(bit_extender_1_out), .Not_op1(not_op_1_not_op1));
  and_op and_op_1 (.op1(bit_extender_1_out), .op2(bit_extender_2_out), .ANDop(and_op_1_andop));
  Mux16x1shiftr mux16x1shiftr_1 (.in_1(bit_extender_1_out), .in_2(Operand2), .out_3(mux16x1shiftr_1_out_3));
  ShiftLeft shiftleft_1 (.A(Operand1), .B(Operand2), .out_3(shiftleft_1_out_3));
  Multiplication multiplication_1 (
    .A4(Operand1[3]), .A3(Operand1[2]), .A2(Operand1[1]), .A1(Operand1[0]), .B1(Operand2[0]),
    .B2(Operand2[1]), .B3(Operand2[2]), .B4(Operand2[3]), .R8(multiplication_1_r1[7]),
    .R7(multiplication_1_r1[6]), .R6(multiplication_1_r1[5]), .R5(multiplication_1_r1[4]),
    .R4(multiplication_1_r1[3]), .R3(multiplication_1_r1[2]), .R2(multiplication_1_r1[1]),
    .R1(multiplication_1_r1[0]));
  Or4bites or4bites_1 (.A(Operand1), .B(Operand2), .out_3(or4bites_1_out_3));
  Four_Bits_Adder four_bits_adder_1 (
    .A1(Operand1[0]), .A2(Operand1[1]), .A3(Operand1[2]), .A4(Operand1[3]), .B1(Operand2[0]),
    .B2(Operand2[1]), .B3(Operand2[2]), .B4(Operand2[3]), .Sum4(four_bits_adder_1_sum1[3]),
    .Cout(four_bits_adder_1_sum1[4]), .Sum1(four_bits_adder_1_sum1[0]), .Sum2(four_bits_adder_1_sum1[1]),
    .Sum3(four_bits_adder_1_sum1[2]));
  Xor4bites xor4bites_1 (.A(Operand1), .B(Operand2), .out_3(xor4bites_1_out_3));
  Four_Bits_Subtractor four_bits_subtractor_1 (
    .A4(Operand1[3]), .A3(Operand1[2]), .A2(Operand1[1]), .A1(Operand1[0]), .B4(Operand2[3]),
    .B3(Operand2[2]), .B2(Operand2[1]), .B1(Operand2[0]), .Sum5(four_bits_subtractor_1_sum1[4]),
    .Sum4(four_bits_subtractor_1_sum1[3]), .Sum3(four_bits_subtractor_1_sum1[2]),
    .Sum2(four_bits_subtractor_1_sum1[1]), .Sum1(four_bits_subtractor_1_sum1[0]));
  Move move_1 (.in_1(Operand1), .out_2(move_1_out_2));
  assign bit_extender_3_out = {{3{1'b0}}, four_bits_adder_1_sum1};  // Bit_Extender bit_extender_3
  assign bit_extender_4_out = {{3{1'b0}}, four_bits_subtractor_1_sum1};  // Bit_Extender bit_extender_4
  assign bit_extender_5_out = {{4{1'b0}}, move_1_out_2};  // Bit_Extender bit_extender_5
  MUX16x1 mux16x1_1 (
    .Out1(Result), .in_1(bit_extender_5_out), .in_2(bit_extender_6_out), .in_3(bit_extender_3_out),
    .in_4(bit_extender_4_out), .in_5(multiplication_1_r1), .in_9(not_op_1_not_op1), .in_10(and_op_1_andop),
    .in_11(or4bites_1_out_3), .in_12(xor4bites_1_out_3), .in_13(shiftleft_1_out_3),
    .in_14(mux16x1shiftr_1_out_3), .in_17(Operation));  // open: in_6, in_7, in_8, in_15, in_16
  assign bit_extender_6_out = {{4{1'b0}}, negative_1_o1};  // Bit_Extender bit_extender_6
endmodule

module MUX2x1 (
  input  [7:0] In0,
  input  [7:0] In1,
  input  S1,
  output [7:0] Out1
);

  wire not_1_out;
  wire [7:0] and_1_out, and_2_out, bit_extender_1_out, bit_extender_2_out;

  not not_1 (not_1_out, S1);
  assign bit_extender_1_out = {{7{not_1_out}}, not_1_out};  // Bit_Extender bit_extender_1
  assign bit_extender_2_out = {{7{S1}}, S1};  // Bit_Extender bit_extender_2
  assign and_1_out = In0 & bit_extender_1_out;  // AND_Gate and_1, 8 bits wide
  assign and_2_out = In1 & bit_extender_2_out;  // AND_Gate and_2, 8 bits wide
  assign Out1 = and_1_out | and_2_out;  // OR_Gate or_1, 8 bits wide
endmodule

module MUX4x1 (
  input  [7:0] In1,
  input  [7:0] in_2,
  input  [7:0] in_3,
  input  [7:0] in_4,
  input  [1:0] in_5,
  output [7:0] Out1
);

  wire [7:0] mux2x1_1_out1, mux2x1_2_out1;

  MUX2x1 mux2x1_1 (.In0(In1), .In1(in_2), .S1(in_5[0]), .Out1(mux2x1_1_out1));
  MUX2x1 mux2x1_2 (.In0(in_3), .In1(in_4), .S1(in_5[0]), .Out1(mux2x1_2_out1));
  MUX2x1 mux2x1_3 (.In0(mux2x1_1_out1), .In1(mux2x1_2_out1), .S1(in_5[1]), .Out1(Out1));
endmodule

module MUX8x1 (
  input  [7:0] In1,
  input  [7:0] in_2,
  input  [7:0] in_3,
  input  [7:0] in_4,
  input  [7:0] in_5,
  input  [7:0] in_6,
  input  [7:0] in_7,
  input  [7:0] in_8,
  input  [2:0] in_9,
  output [7:0] Out1
);

  wire [7:0] mux4x1_1_out1, mux4x1_2_out1;

  MUX4x1 mux4x1_1 (.In1(In1), .in_2(in_2), .in_3(in_3), .in_4(in_4), .in_5(in_9[1:0]), .Out1(mux4x1_1_out1));
  MUX4x1 mux4x1_2 (.In1(in_5), .in_2(in_6), .in_3(in_7), .in_4(in_8), .in_5(in_9[1:0]), .Out1(mux4x1_2_out1));
  MUX2x1 mux2x1_1 (.In0(mux4x1_1_out1), .In1(mux4x1_2_out1), .S1(in_9[2]), .Out1(Out1));
endmodule

module MUX16x1 (
  input  [7:0] in_1,
  input  [7:0] in_2,
  input  [7:0] in_3,
  input  [7:0] in_4,
  input  [7:0] in_5,
  input  [7:0] in_6,
  input  [7:0] in_7,
  input  [7:0] in_8,
  input  [7:0] in_9,
  input  [7:0] in_10,
  input  [7:0] in_11,
  input  [7:0] in_12,
  input  [7:0] in_13,
  input  [7:0] in_14,
  input  [7:0] in_15,
  input  [7:0] in_16,
  input  [3:0] in_17,
  output [7:0] Out1
);

  wire [7:0] mux8x1_1_out1, mux8x1_2_out1;

  MUX8x1 mux8x1_1 (
    .In1(in_1), .in_2(in_2), .in_3(in_3), .in_4(in_4), .in_5(in_5), .in_6(in_6), .in_7(in_7), .in_8(in_8),
    .in_9(in_17[2:0]), .Out1(mux8x1_1_out1));
  MUX8x1 mux8x1_2 (
    .In1(in_9), .in_2(in_10), .in_3(in_11), .in_4(in_12), .in_5(in_13), .in_6(in_14), .in_7(in_15),
    .in_8(in_16), .in_9(in_17[2:0]), .Out1(mux8x1_2_out1));
  MUX2x1 mux2x1_1 (.In0(mux8x1_1_out1), .In1(mux8x1_2_out1), .S1(in_17[3]), .Out1(Out1));
endmodule

module not_op (
  input  [7:0] op1,
  output [7:0] Not_op1
);

  assign Not_op1 = ~op1;  // NOT_Gate not_1, 8 bits wide
endmodule

module and_op (
  input  [7:0] op1,
  input  [7:0] op2,
  output [7:0] ANDop
);

  assign ANDop = op1 & op2;  // AND_Gate and_1, 8 bits wide
endmodule

module shift_r_1 (
  input  [7:0] in_1,
  output [7:0] out_2
);


  assign out_2 = {{5{1'b0}}, in_1[3:1]};
endmodule

module shift_r_2 (
  input  [7:0] in_1,
  output [7:0] out_2
);


  assign out_2 = {{6{1'b0}}, in_1[3:2]};
endmodule

module shift_r_3 (
  input  [7:0] in_1,
  output [7:0] out_2
);


  assign out_2 = {{7{1'b0}}, in_1[3]};
endmodule

module Mux16x1shiftr (
  input  [7:0] in_1,
  input  [3:0] in_2,
  output [7:0] out_3
);

  wire [7:0] shift_r_0_1_out_2, shift_r_1_1_out_2, shift_r_2_1_out_2, shift_r_3_1_out_2;

  shift_r_0 shift_r_0_1 (.in_1(in_1), .out_2(shift_r_0_1_out_2));
  shift_r_1 shift_r_1_1 (.in_1(in_1), .out_2(shift_r_1_1_out_2));
  shift_r_2 shift_r_2_1 (.in_1(in_1), .out_2(shift_r_2_1_out_2));
  shift_r_3 shift_r_3_1 (.in_1(in_1), .out_2(shift_r_3_1_out_2));
  MUX16x1_2 mux16x1_2_1 (
    .in_1(shift_r_0_1_out_2), .in_2(shift_r_1_1_out_2), .in_3(shift_r_2_1_out_2), .in_4(shift_r_3_1_out_2),
    .in_5({8{1'b0}}), .in_6({8{1'b0}}), .in_7({8{1'b0}}), .in_8({8{1'b0}}), .in_9({8{1'b0}}),
    .in_10({8{1'b0}}), .in_11({8{1'b0}}), .in_12({8{1'b0}}), .in_13({8{1'b0}}), .in_14({8{1'b0}}),
    .in_15({8{1'b0}}), .in_16({8{1'b0}}), .in_17(in_2), .Out1(out_3));
endmodule

module shift_r_0 (
  input  [7:0] in_1,
  output [7:0] out_2
);


  assign out_2 = {4'b0000, in_1[3:0]};
endmodule

module MUX16x1_2 (
  input  [7:0] in_1,
  input  [7:0] in_2,
  input  [7:0] in_3,
  input  [7:0] in_4,
  input  [7:0] in_5,
  input  [7:0] in_6,
  input  [7:0] in_7,
  input  [7:0] in_8,
  input  [7:0] in_9,
  input  [7:0] in_10,
  input  [7:0] in_11,
  input  [7:0] in_12,
  input  [7:0] in_13,
  input  [7:0] in_14,
  input  [7:0] in_15,
  input  [7:0] in_16,
  input  [3:0] in_17,
  output [7:0] Out1
);

  wire [7:0] mux8x1_1_out1, mux8x1_2_out1;

  MUX8x1 mux8x1_1 (
    .In1(in_1), .in_2(in_2), .in_3(in_3), .in_4(in_4), .in_5(in_5), .in_6(in_6), .in_7(in_7), .in_8(in_8),
    .in_9(in_17[2:0]), .Out1(mux8x1_1_out1));
  MUX8x1 mux8x1_2 (
    .In1(in_9), .in_2(in_10), .in_3(in_11), .in_4(in_12), .in_5(in_13), .in_6(in_14), .in_7(in_15),
    .in_8(in_16), .in_9(in_17[2:0]), .Out1(mux8x1_2_out1));
  MUX2x1 mux2x1_1 (.In0(mux8x1_1_out1), .In1(mux8x1_2_out1), .S1(in_17[3]), .Out1(Out1));
endmodule

module Half_Adder (
  input  A,
  input  B,
  output Sum,
  output Carry
);

  xor xor_1 (Sum, A, B);
  and and_1 (Carry, A, B);
endmodule

// FA
module Full_Adder (
  input  A,
  input  B,
  input  Cin,
  output Sum,
  output Carry
);

  wire half_adder_1_carry, half_adder_1_sum, half_adder_2_carry;

  Half_Adder half_adder_1 (.A(A), .B(B), .Sum(half_adder_1_sum), .Carry(half_adder_1_carry));
  or or_1 (Carry, half_adder_2_carry, half_adder_1_carry);
  Half_Adder half_adder_2 (.A(half_adder_1_sum), .B(Cin), .Sum(Sum), .Carry(half_adder_2_carry));
endmodule

module Multiplication (
  input  A4,
  input  A3,
  input  A2,
  input  A1,
  input  B1,
  input  B2,
  input  B3,
  input  B4,
  output R8,
  output R7,
  output R6,
  output R5,
  output R4,
  output R3,
  output R2,
  output R1
);

  wire and_1_out, and_2_out, and_3_out, and_4_out, and_5_out, and_6_out, and_7_out, and_8_out, and_9_out,
       and_10_out, and_11_out, and_12_out, and_13_out, and_14_out, and_15_out, b2h_1_c, b2h_1_d, b2h_1_e,
       b2h_1_f, b2h_1_g, b2h_1_out_5, b2h_1_out_6, b2h_2_c, b2h_2_d, b2h_2_e, b2h_2_f, b2h_2_g, b2h_2_out_5,
       b2h_2_out_6, four_bits_adder_subtractor_1_sum2, four_bits_adder_subtractor_1_sum3,
       four_bits_adder_subtractor_1_sum4, four_bits_adder_subtractor_1_sum5,
       four_bits_adder_subtractor_3_sum2, four_bits_adder_subtractor_3_sum3,
       four_bits_adder_subtractor_3_sum4, four_bits_adder_subtractor_3_sum5;

  and and_1 (and_1_out, B4, A4);
  and and_2 (and_2_out, B3, A4);
  and and_3 (and_3_out, B2, A4);
  and and_4 (and_4_out, B4, A3);
  and and_5 (and_5_out, B2, A3);
  and and_6 (and_6_out, B3, A3);
  and and_7 (and_7_out, B4, A2);
  and and_8 (and_8_out, B3, A2);
  and and_9 (and_9_out, B2, A2);
  and and_10 (and_10_out, B4, A1);
  and and_11 (and_11_out, B3, A1);
  and and_12 (and_12_out, B2, A1);
  Four_Bits_Adder_Subtractor four_bits_adder_subtractor_1 (
    .B4(and_2_out), .A4(four_bits_adder_subtractor_3_sum5), .B3(and_6_out),
    .A3(four_bits_adder_subtractor_3_sum4), .B2(and_8_out), .A2(four_bits_adder_subtractor_3_sum3),
    .B1(and_11_out), .A1(four_bits_adder_subtractor_3_sum2), .Sum5(four_bits_adder_subtractor_1_sum5),
    .Sum4(four_bits_adder_subtractor_1_sum4), .Sum3(four_bits_adder_subtractor_1_sum3),
    .Sum2(four_bits_adder_subtractor_1_sum2), .Sum1(R3), .Control(1'b0));
  Four_Bits_Adder_Subtractor four_bits_adder_subtractor_2 (
    .B4(and_1_out), .A4(four_bits_adder_subtractor_1_sum5), .B3(and_4_out),
    .A3(four_bits_adder_subtractor_1_sum4), .B2(and_7_out), .A2(four_bits_adder_subtractor_1_sum3),
    .B1(and_10_out), .A1(four_bits_adder_subtractor_1_sum2), .Sum5(R8), .Sum4(R7), .Sum3(R6), .Sum2(R5),
    .Sum1(R4), .Control(1'b0));
  and and_13 (and_13_out, A4, B1);
  Four_Bits_Adder_Subtractor four_bits_adder_subtractor_3 (
    .B4(and_3_out), .A4(1'b0), .B3(and_5_out), .A3(and_13_out), .B2(and_9_out), .A2(and_14_out),
    .B1(and_12_out), .A1(and_15_out), .Sum5(four_bits_adder_subtractor_3_sum5),
    .Sum4(four_bits_adder_subtractor_3_sum4), .Sum3(four_bits_adder_subtractor_3_sum3),
    .Sum2(four_bits_adder_subtractor_3_sum2), .Sum1(R2), .Control(1'b0));
  b2h b2h_1 (
    .A(R8), .B(R7), .in_3(R6), .in_4(R5), .out_5(b2h_1_out_5), .out_6(b2h_1_out_6), .c(b2h_1_c), .d(b2h_1_d),
    .e(b2h_1_e), .f(b2h_1_f), .g(b2h_1_g));
  and and_14 (and_14_out, A3, B1);
  _7_Segment_Display #(.decimalPoint("false")) u_7_segment_display_1 (
    .g(b2h_1_g), .f(b2h_1_f), .a(b2h_1_out_5), .b(b2h_1_out_6), .e(b2h_1_e), .d(b2h_1_d), .c(b2h_1_c));
  and and_15 (and_15_out, A2, B1);
  _7_Segment_Display #(.decimalPoint("false")) u_7_segment_display_2 (
    .g(b2h_2_g), .f(b2h_2_f), .a(b2h_2_out_5), .b(b2h_2_out_6), .e(b2h_2_e), .d(b2h_2_d), .c(b2h_2_c));
  b2h b2h_2 (
    .A(R4), .B(R3), .in_3(R2), .in_4(R1), .out_5(b2h_2_out_5), .out_6(b2h_2_out_6), .c(b2h_2_c), .d(b2h_2_d),
    .e(b2h_2_e), .f(b2h_2_f), .g(b2h_2_g));
  and and_16 (R1, B1, A1);
endmodule

// 4-Bit Adder
module Four_Bits_Adder_Subtractor (
  input  A4,
  input  A3,
  input  A2,
  input  A1,
  input  B4,
  input  B3,
  input  B2,
  input  B1,
  input  Control,
  output Sum5,
  output Sum4,
  output Sum3,
  output Sum2,
  output Sum1
);

  wire full_adder_2_carry, full_adder_3_carry, full_adder_4_carry, xor_1_out, xor_2_out, xor_3_out, xor_4_out;

  xor xor_1 (xor_1_out, B4, Control);
  Full_Adder full_adder_1 (.A(A4), .B(xor_1_out), .Cin(full_adder_2_carry), .Sum(Sum4), .Carry(Sum5));
  xor xor_2 (xor_2_out, B3, Control);
  Full_Adder full_adder_2 (.A(A3), .B(xor_2_out), .Cin(full_adder_3_carry), .Sum(Sum3), .Carry(full_adder_2_carry));
  xor xor_3 (xor_3_out, B2, Control);
  Full_Adder full_adder_3 (.A(A2), .B(xor_3_out), .Cin(full_adder_4_carry), .Sum(Sum2), .Carry(full_adder_3_carry));
  xor xor_4 (xor_4_out, B1, Control);
  Full_Adder full_adder_4 (.A(A1), .B(xor_4_out), .Cin(Control), .Sum(Sum1), .Carry(full_adder_4_carry));
endmodule

// B2H
module b2h (
  input  A,
  input  B,
  input  in_3,
  input  in_4,
  output out_5,
  output out_6,
  output c,
  output d,
  output e,
  output f,
  output g
);

  wire and_1_out, and_2_out, and_3_out, and_4_out, and_5_out, and_6_out, and_7_out, and_8_out, and_9_out,
       and_10_out, and_11_out, and_12_out, and_13_out, and_14_out, and_15_out, and_16_out, and_17_out,
       and_18_out, and_19_out, and_20_out, and_21_out, and_22_out, and_23_out, and_24_out, and_25_out,
       and_26_out, and_27_out, and_28_out, and_29_out, and_30_out, and_31_out, and_32_out, and_33_out,
       and_34_out, and_35_out, not_1_out, not_2_out, not_3_out, not_4_out;

  not not_1 (not_1_out, A);
  not not_2 (not_2_out, B);
  not not_3 (not_3_out, in_3);
  not not_4 (not_4_out, in_4);
  and and_1 (and_1_out, not_2_out, not_4_out);
  and and_2 (and_2_out, not_1_out, in_3);
  and and_3 (and_3_out, not_1_out, B, in_4);
  and and_4 (and_4_out, B, in_3);
  and and_5 (and_5_out, A, not_2_out, not_3_out);
  and and_6 (and_6_out, A, not_4_out);
  and and_7 (and_7_out, not_1_out, not_2_out);
  and and_8 (and_8_out, not_1_out, not_3_out, not_4_out);
  and and_9 (and_9_out, not_2_out, not_4_out);
  and and_10 (and_10_out, not_1_out, in_3, in_4);
  and and_11 (and_11_out, A, not_3_out, in_4);
  and and_12 (and_12_out, not_1_out, not_3_out);
  and and_13 (and_13_out, not_1_out, in_4);
  and and_14 (and_14_out, not_3_out, in_4);
  and and_15 (and_15_out, not_1_out, B);
  and and_16 (and_16_out, A, not_2_out);
  and and_17 (and_17_out, not_1_out, not_2_out, not_4_out);
  and and_18 (and_18_out, not_2_out, in_3, in_4);
  and and_19 (and_19_out, B, not_3_out, in_4);
  and and_20 (and_20_out, B, in_3, not_4_out);
  and and_21 (and_21_out, A, not_3_out);
  and and_22 (and_22_out, not_2_out, not_4_out);
  and and_23 (and_23_out, in_3, not_4_out);
  and and_24 (and_24_out, A, in_3);
  and and_25 (and_25_out, A, B);
  and and_26 (and_26_out, not_3_out, not_4_out);
  and and_27 (and_27_out, not_1_out, B, not_3_out);
  and and_28 (and_28_out, B, not_4_out);
  and and_29 (and_29_out, A, not_2_out);
  and and_30 (and_30_out, A, in_3);
  and and_31 (and_31_out, not_2_out, in_3);
  and and_32 (and_32_out, in_3, not_4_out);
  and and_33 (and_33_out, not_1_out, B, not_3_out);
  and and_34 (and_34_out, A, not_2_out);
  and and_35 (and_35_out, A, in_4);
  or or_1 (out_5, and_1_out, and_2_out, and_3_out, and_4_out, and_5_out, and_6_out);
  or or_2 (out_6, and_7_out, and_8_out, and_9_out, and_10_out, and_11_out);
  or or_3 (c, and_12_out, and_13_out, and_14_out, and_15_out, and_16_out);
  or or_4 (d, and_17_out, and_18_out, and_19_out, and_20_out, and_21_out);
  or or_5 (e, and_22_out, and_23_out, and_24_out, and_25_out);
  or or_6 (f, and_26_out, and_27_out, and_28_out, and_29_out, and_30_out);
  or or_7 (g, and_31_out, and_32_out, and_33_out, and_34_out, and_35_out);
endmodule

module Four_Bits_Adder (
  input  A1,
  input  A2,
  input  A3,
  input  A4,
  input  B1,
  input  B2,
  input  B3,
  input  B4,
  output Sum4,
  output Cout,
  output Sum1,
  output Sum2,
  output Sum3
);

  wire full_adder_1_carry, full_adder_2_carry, full_adder_3_carry;

  Full_Adder full_adder_1 (.A(A1), .B(B1), .Cin(1'b0), .Sum(Sum1), .Carry(full_adder_1_carry));
  Full_Adder full_adder_2 (.A(A2), .B(B2), .Cin(full_adder_1_carry), .Sum(Sum2), .Carry(full_adder_2_carry));
  Full_Adder full_adder_3 (.A(A3), .B(B3), .Cin(full_adder_2_carry), .Sum(Sum3), .Carry(full_adder_3_carry));
  Full_Adder full_adder_4 (.A(A4), .B(B4), .Cin(full_adder_3_carry), .Sum(Sum4), .Carry(Cout));
endmodule

module Four_Bits_Subtractor (
  input  A4,
  input  A3,
  input  A2,
  input  A1,
  input  B4,
  input  B3,
  input  B2,
  input  B1,
  output Sum5,
  output Sum4,
  output Sum3,
  output Sum2,
  output Sum1
);

  wire full_adder_2_carry, full_adder_3_carry, full_adder_4_carry, xor_1_out, xor_2_out, xor_3_out, xor_4_out;

  xor xor_1 (xor_1_out, B4, 1'b1);
  Full_Adder full_adder_1 (.A(A4), .B(xor_1_out), .Cin(full_adder_2_carry), .Sum(Sum4), .Carry(Sum5));
  xor xor_2 (xor_2_out, B3, 1'b1);
  Full_Adder full_adder_2 (.A(A3), .B(xor_2_out), .Cin(full_adder_3_carry), .Sum(Sum3), .Carry(full_adder_2_carry));
  xor xor_3 (xor_3_out, B2, 1'b1);
  Full_Adder full_adder_3 (.A(A2), .B(xor_3_out), .Cin(full_adder_4_carry), .Sum(Sum2), .Carry(full_adder_3_carry));
  xor xor_4 (xor_4_out, B1, 1'b1);
  Full_Adder full_adder_4 (.A(A1), .B(xor_4_out), .Cin(1'b1), .Sum(Sum1), .Carry(full_adder_4_carry));

  // Notes on the sheet:
  //   Sum5 is ignored.
endmodule

module ShiftLeft1 (
  input  [3:0] A,
  output [7:0] out_2
);


  assign out_2 = {3'b000, A, 1'b0};
endmodule

module ShigtLeft0 (
  input  [3:0] in_1,
  output [7:0] out_2
);


  assign out_2 = {4'b0000, in_1};

  // Notes on the sheet:
  //   A
endmodule

module ShiftLeft2 (
  input  [3:0] in_1,
  output [7:0] out_2
);


  assign out_2 = {2'b00, in_1, 2'b00};
endmodule

module ShiftLeft3 (
  input  [3:0] in_1,
  output [7:0] out_2
);


  assign out_2 = {1'b0, in_1, 3'b000};
endmodule

module Shiftleft4 (
  input  [3:0] in_1,
  output [7:0] out_2
);


  assign out_2 = {in_1, 4'b0000};
endmodule

module ShiftLeft5 (
  input  [3:0] in_1,
  output [7:0] out_2
);


  assign out_2 = {in_1[2:0], {5{1'b0}}};
endmodule

module ShiftLeft6 (
  input  [3:0] in_1,
  output [7:0] out_2
);


  assign out_2 = {in_1[1:0], {6{1'b0}}};
endmodule

module ShiftLeft7 (
  input  [3:0] in_1,
  output [7:0] out_2
);


  assign out_2 = {in_1[0], {7{1'b0}}};
endmodule

module Or4bites (
  input  [3:0] A,
  input  [3:0] B,
  output [7:0] out_3
);

  wire [3:0] or_1_out;

  assign or_1_out = A | B;  // OR_Gate or_1, 4 bits wide
  assign out_3 = {{4{1'b0}}, or_1_out};  // Bit_Extender bit_extender_1
endmodule

module Xor4bites (
  input  [3:0] A,
  input  [3:0] B,
  output [7:0] out_3
);

  wire [3:0] xor_1_out;

  assign xor_1_out = A ^ B;  // XOR_Gate xor_1, 4 bits wide
  assign out_3 = {{4{1'b0}}, xor_1_out};  // Bit_Extender bit_extender_1
endmodule

module Mux4x1ForShiftingLeft (
  input  [7:0] in_1,
  input  [7:0] in_2,
  input  [7:0] in_3,
  input  [7:0] in_4,
  input  [1:0] in_5,
  output [7:0] out_6
);

  wire [7:0] mux2x1forshiftingleft_1_out_4, mux2x1forshiftingleft_2_out_4;

  Mux2x1ForShiftingLeft mux2x1forshiftingleft_1 (
    .I0(in_1), .I1(in_2), .S(in_5[0]), .out_4(mux2x1forshiftingleft_1_out_4));
  Mux2x1ForShiftingLeft mux2x1forshiftingleft_2 (
    .I0(in_3), .I1(in_4), .S(in_5[0]), .out_4(mux2x1forshiftingleft_2_out_4));
  Mux2x1ForShiftingLeft mux2x1forshiftingleft_3 (
    .I0(mux2x1forshiftingleft_1_out_4), .I1(mux2x1forshiftingleft_2_out_4), .S(in_5[1]), .out_4(out_6));
endmodule

module Mux8x1ForShiftingLeft (
  input  [7:0] in_1,
  input  [7:0] in_2,
  input  [7:0] in_3,
  input  [7:0] in_4,
  input  [7:0] in_5,
  input  [7:0] in_6,
  input  [7:0] in_7,
  input  [7:0] in_8,
  input  [2:0] in_9,
  output [7:0] out_10
);

  wire [7:0] mux4x1forshiftingleft_1_out_6, mux4x1forshiftingleft_2_out_6;

  Mux4x1ForShiftingLeft mux4x1forshiftingleft_1 (
    .in_1(in_1), .in_2(in_2), .in_3(in_3), .in_4(in_4), .in_5(in_9[1:0]),
    .out_6(mux4x1forshiftingleft_1_out_6));
  Mux4x1ForShiftingLeft mux4x1forshiftingleft_2 (
    .in_1(in_5), .in_2(in_6), .in_3(in_7), .in_4(in_8), .in_5(in_9[1:0]),
    .out_6(mux4x1forshiftingleft_2_out_6));
  Mux2x1ForShiftingLeft mux2x1forshiftingleft_1 (
    .I0(mux4x1forshiftingleft_1_out_6), .I1(mux4x1forshiftingleft_2_out_6), .S(in_9[2]), .out_4(out_10));
endmodule

module Mux1x16ForShiftingLeft (
  input  [7:0] in_1,
  input  [7:0] in_2,
  input  [7:0] in_3,
  input  [7:0] in_4,
  input  [7:0] in_5,
  input  [7:0] in_6,
  input  [7:0] in_7,
  input  [7:0] in_8,
  input  [7:0] in_9,
  input  [7:0] in_10,
  input  [7:0] in_11,
  input  [7:0] in_12,
  input  [7:0] in_13,
  input  [7:0] in_14,
  input  [7:0] in_15,
  input  [7:0] in_16,
  input  [3:0] in_17,
  output [7:0] out_18
);

  wire [7:0] mux8x1forshiftingleft_1_out_10, mux8x1forshiftingleft_2_out_10;

  Mux8x1ForShiftingLeft mux8x1forshiftingleft_1 (
    .in_1(in_1), .in_2(in_2), .in_3(in_3), .in_4(in_4), .in_5(in_5), .in_6(in_6), .in_7(in_7), .in_8(in_8),
    .in_9(in_17[2:0]), .out_10(mux8x1forshiftingleft_1_out_10));
  Mux8x1ForShiftingLeft mux8x1forshiftingleft_2 (
    .in_1(in_9), .in_2(in_10), .in_3(in_11), .in_4(in_12), .in_5(in_13), .in_6(in_14), .in_7(in_15),
    .in_8(in_16), .in_9(in_17[2:0]), .out_10(mux8x1forshiftingleft_2_out_10));
  Mux2x1ForShiftingLeft mux2x1forshiftingleft_1 (
    .I0(mux8x1forshiftingleft_1_out_10), .I1(mux8x1forshiftingleft_2_out_10), .S(in_17[3]), .out_4(out_18));
endmodule

module Mux2x1ForShiftingLeft (
  input  [7:0] I0,
  input  [7:0] I1,
  input  S,
  output [7:0] out_4
);

  wire not_1_out;
  wire [7:0] and_1_out, and_2_out, bit_extender_1_out, bit_extender_2_out;

  not not_1 (not_1_out, S);
  assign bit_extender_1_out = {{7{not_1_out}}, not_1_out};  // Bit_Extender bit_extender_1
  assign bit_extender_2_out = {{7{S}}, S};  // Bit_Extender bit_extender_2
  assign and_1_out = I0 & bit_extender_1_out;  // AND_Gate and_1, 8 bits wide
  assign and_2_out = I1 & bit_extender_2_out;  // AND_Gate and_2, 8 bits wide
  assign out_4 = and_1_out | and_2_out;  // OR_Gate or_1, 8 bits wide
endmodule

module ShiftLeft (
  input  [3:0] A,
  input  [3:0] B,
  output [7:0] out_3
);

  wire [7:0] shiftleft1_1_out_2, shiftleft2_1_out_2, shiftleft3_1_out_2, shiftleft4_1_out_2,
       shiftleft5_1_out_2, shiftleft6_1_out_2, shiftleft7_1_out_2, shigtleft0_1_out_2;

  ShigtLeft0 shigtleft0_1 (.in_1(A), .out_2(shigtleft0_1_out_2));
  ShiftLeft1 shiftleft1_1 (.A(A), .out_2(shiftleft1_1_out_2));
  ShiftLeft2 shiftleft2_1 (.in_1(A), .out_2(shiftleft2_1_out_2));
  ShiftLeft3 shiftleft3_1 (.in_1(A), .out_2(shiftleft3_1_out_2));
  Shiftleft4 shiftleft4_1 (.in_1(A), .out_2(shiftleft4_1_out_2));
  ShiftLeft5 shiftleft5_1 (.in_1(A), .out_2(shiftleft5_1_out_2));
  ShiftLeft6 shiftleft6_1 (.in_1(A), .out_2(shiftleft6_1_out_2));
  ShiftLeft7 shiftleft7_1 (.in_1(A), .out_2(shiftleft7_1_out_2));
  Mux1x16ForShiftingLeft mux1x16forshiftingleft_1 (
    .in_1(shigtleft0_1_out_2), .in_2(shiftleft1_1_out_2), .in_3(shiftleft2_1_out_2),
    .in_4(shiftleft3_1_out_2), .in_5(shiftleft4_1_out_2), .in_6(shiftleft5_1_out_2),
    .in_7(shiftleft6_1_out_2), .in_8(shiftleft7_1_out_2), .in_9({8{1'b0}}), .in_10({8{1'b0}}),
    .in_11({8{1'b0}}), .in_12({8{1'b0}}), .in_13({8{1'b0}}), .in_14({8{1'b0}}), .in_15({8{1'b0}}),
    .in_16({8{1'b0}}), .in_17(B), .out_18(out_3));
endmodule

module MainCircuits (
  input  [3:0] in_1,
  input  [3:0] in_2,
  input  [3:0] in_3,
  input  [3:0] in_4,
  input  [3:0] in_5,
  input  [3:0] in_6,
  output [7:0] out_7,
  output [7:0] out_8,
  output [7:0] out_9
);

  ShiftLeft shiftleft_1 (.A(in_1), .B(in_2), .out_3(out_7));
  Or4bites or4bites_1 (.A(in_3), .B(in_4), .out_3(out_8));
  Xor4bites xor4bites_1 (.A(in_5), .B(in_6), .out_3(out_9));
endmodule

module Move (
  input  [3:0] in_1,
  output [3:0] out_2
);


  assign out_2 = in_1;
endmodule

module Negative (
  input  A4,
  input  A3,
  input  A2,
  input  A1,
  output O4,
  output O3,
  output O2,
  output O1
);

  wire and_1_out, and_2_out, and_3_out, not_1_out, not_2_out, not_3_out, not_4_out;

  not not_1 (not_1_out, A4);
  xor xor_1 (O4, not_1_out, and_1_out);
  and and_1 (and_1_out, not_2_out, and_2_out);
  not not_2 (not_2_out, A3);
  xor xor_2 (O3, not_2_out, and_2_out);
  and and_2 (and_2_out, not_3_out, and_3_out);
  not not_3 (not_3_out, A2);
  and and_3 (and_3_out, not_4_out, 1'b1);
  xor xor_3 (O2, not_3_out, and_3_out);
  not not_4 (not_4_out, A1);
  xor xor_4 (O1, not_4_out, 1'b1);
endmodule

module complement (
  input  A4,
  input  A3,
  input  A2,
  input  A1,
  output O4,
  output O3,
  output O2,
  output O1
);

  wire and_1_out, and_2_out, and_3_out, not_1_out, not_2_out, not_3_out, not_4_out;

  not not_1 (not_1_out, A4);
  xor xor_1 (O4, not_1_out, and_1_out);
  and and_1 (and_1_out, not_2_out, and_2_out);
  not not_2 (not_2_out, A3);
  xor xor_2 (O3, not_2_out, and_2_out);
  and and_2 (and_2_out, not_3_out, and_3_out);
  not not_3 (not_3_out, A2);
  and and_3 (and_3_out, not_4_out, 1'b1);
  xor xor_3 (O2, not_3_out, and_3_out);
  not not_4 (not_4_out, A1);
  xor xor_4 (O1, not_4_out, 1'b1);
endmodule
